# Fritzing sketch Controller (saved by Fritzing 0.9.1b)

parts:
  Part1 = Arduino Uno (Rev3)  # not connected
  Part2 = Adafruit Proto Shield for Arduino Kit - v.5
  J2 = Piezo Speaker  # not connected
  Part3 = Bluetooth HC-05 Macho  # not connected
  JP2 = Header 1 [package=1x01_offset]  # not connected
  JP3 = Header 1 [package=1x01_offset]  # not connected
  JP4 = Header 1 [package=1x01_offset]  # not connected
  JP5 = Header 1 [package=1x01_offset]  # not connected
  JP6 = Header 1 [package=1x01_offset]
  JP7 = Header 1 [package=1x01_offset]
  JP8 = Header 1 [package=1x01_offset]
  JP9 = Header 1 [package=1x01_offset]
  JP10 = Header 1 [package=1x01_offset]
  JP11 = Header 1 [package=1x01_offset]
  JP12 = Header 1 [package=1x01_offset]
  JP13 = Header 1 [package=1x01_offset]
  JP14 = Header 1 [package=1x01_offset]
  JP15 = Header 1 [package=1x01_offset]
  JP16 = Header 1 [package=1x01_offset]  # not connected
  JP17 = Header 1 [package=1x01_offset]  # not connected
  JP18 = Header 1 [package=1x01_offset]  # not connected
  JP19 = Header 1 [package=1x01_offset]  # not connected
  JP20 = Header 1 [package=1x01_offset]  # not connected
  JP21 = Header 1 [package=1x01_offset]  # not connected
  JP22 = Header 1 [package=1x01_offset]  # not connected
  JP23 = Header 1 [package=1x01_offset]  # not connected
  JP24 = Header 1 [package=1x01_offset]
  JP25 = Header 1 [package=1x01_offset]
  JP26 = Header 1 [package=1x01_offset]
  JP27 = Header 1 [package=1x01_offset]
  JP28 = Header 1 [package=1x01_offset]
  JP29 = Header 1 [package=1x01_offset]
  JP30 = Header 1 [package=1x01_offset]  # not connected
  JP31 = Header 1 [package=1x01_offset]  # not connected
  JP32 = Header 1 [package=1x01_offset]  # not connected
  JP33 = Header 1 [package=1x01_offset]  # not connected
  JP34 = Header 1 [package=1x01_offset]  # not connected
  JP35 = Header 1 [package=1x01_offset]  # not connected
  JP36 = Header 1 [package=1x01_offset]  # not connected
  JP37 = Header 1 [package=1x01_offset]  # not connected
  JP46 = Header 1 [package=1x01_offset]
  JP47 = Header 1 [package=1x01_offset]
  JP48 = Header 1 [package=1x01_offset]
  JP49 = Header 1 [package=1x01_offset]
  JP50 = Header 1 [package=1x01_offset]
  JP51 = Header 1 [package=1x01_offset]
  JP52 = Header 1 [package=1x01_offset]
  JP53 = Header 1 [package=1x01_offset]
  JP54 = Header 1 [package=1x01_offset]
  JP55 = Header 1 [package=1x01_offset]
  JP56 = Header 1 [package=1x01_offset]
  JP57 = Header 1 [package=1x01_offset]
  JP58 = Header 1 [package=1x01_offset]
  JP59 = Header 1 [package=1x01_offset]
  JP60 = Header 1 [package=1x01_offset]
  JP61 = Header 1 [package=1x01_offset]
  JP62 = Header 1 [package=1x01_offset]  # not connected
  JP63 = Header 1 [package=1x01_offset]
  JP64 = Header 1 [package=1x01_offset]
  JP65 = Header 1 [package=1x01_offset]
  JP66 = Header 1 [package=1x01_offset]
  JP67 = Header 1 [package=1x01_offset]
  JP68 = Header 1 [package=1x01_offset]

nets:
  N1: Part2.AREF, JP46.1
  N2: Part2.GND, Part2.P$1#210, Part2.P$2#211, Part2.P$4#213, Part2.P$5#214, JP6.1, JP7.1, JP8.1, JP9.1, JP10.1, JP27.1, JP29.1, JP51.1
  N3: Part2.D13, JP47.1
  N4: Part2.D12, JP53.1
  N5: Part2.D11, JP52.1
  N6: Part2.D10, JP50.1
  N7: Part2.D9, JP48.1
  N8: Part2.D8, JP49.1
  N9: Part2.D0, JP57.1
  N10: Part2.D1, JP56.1
  N11: Part2.D2, JP58.1
  N12: Part2.D3, JP60.1
  N13: Part2.D4, JP61.1
  N14: Part2.D5, JP55.1
  N15: Part2.D6, JP59.1
  N16: Part2.D7, JP54.1
  N17: Part2.VIN, JP28.1
  N18: Part2.+5V, Part2.P$1#200, Part2.P$2#201, Part2.P$4#203, Part2.P$5#204, JP11.1, JP12.1, JP13.1, JP14.1, JP15.1, JP24.1
  N19: Part2.3.3V, JP26.1
  N20: Part2.RESET, JP25.1
  N21: Part2.A5, JP66.1
  N22: Part2.A4, JP63.1
  N23: Part2.A3, JP65.1
  N24: Part2.A2, JP67.1
  N25: Part2.A1, JP64.1
  N26: Part2.A0, JP68.1

custom parts:
  Adafruit Proto Shield for Arduino Kit - v.5: Arduino prototyping shield designed by Adafruit Industries
