# Fritzing sketch Robot (saved by Fritzing 0.9.1b)
perfboards: 1
breadboards: 1

parts:
  Part1 = HC-SR04 Ultrasonic Rangemeter
  M1 = DC Motor
  M2 = DC Motor
  LM35_TempSensor1 = LM35 TempSensor
  LCD1 = LCD screen
  VCC1 = 4 x AAA Battery Mount
  Part2 = Arduino Uno (Rev3)
  Part3 = 2A MOTOR SHIELD 9
  U1 = SWITCH_SPDT [package=kps-1290]
  Part6 = Bluetooth HC-05 Macho
  RE1 = Rotary Encoder [package=THT]
  Part8 = Arduino Prototyping Shield
  R2 = Resistor [tolerance=±5% resistance=2.0k package=THT]
  R3 = Resistor [tolerance=±5% resistance=1k package=THT]
  RE4 = Rotary Encoder [package=THT]

nets:
  N1: Part1.VCC, Part8.N$67
  N2: Part1.Trig, Part8.D8
  N3: Part1.Echo, Part8.A3
  N4: Part1.GND, Part8.N$76
  N5: M1.pin_1, Part3.M1+
  N6: M1.pin_2, Part3.M1-
  N7: M2.pin_1, Part3.M2+
  N8: M2.pin_2, Part3.M2-
  N9: LM35_TempSensor1.POWER, Part8.N$34
  N10: LM35_TempSensor1.GND, Part8.A2
  N11: LM35_TempSensor1.INPUT, Part8.N$27
  VSS: LCD1.VSS, LCD1.VDD, LCD1.V0
  N12: LCD1.RS, LCD1.R/W, LCD1.E
  N13: LCD1.DB4, LCD1.DB5, LCD1.DB6
  N14: LCD1.DB7, LCD1.LED+, LCD1.LED-
  N15: VCC1.-, Part3.GND#0
  N16: VCC1.+, U1.O
  N17: Part2.A0, Part3.A0
  N18: Part2.A1, Part3.A1
  N19: Part2.A2, Part3.A2
  N20: Part2.A3, Part3.A3
  N21: Part2.A4/SDA, Part3.A4
  N22: Part2.A5/SCL, Part3.A5
  N23: Part2.D8, Part3.D8
  N24: Part2.D9_PWM, Part3.D9
  N25: Part2.D10_PWM/SS, Part3.D10
  N26: Part2.D11_PWM/MOSI, Part3.D11
  N27: Part2.D12/MISO, Part3.D12
  N28: Part2.D13/SCK, Part3.D13
  N29: Part2.GND, Part3.GND#connector1pad-0-1-1-48-61, Part3.GND#connector1pad-0-1-9-9-4-9, Part3.GND#connector1pad-4-5-0-39-8-14
  N30: Part2.AREF, Part3.AFER
  N31: Part2.D1/TX, Part3.D1
  N32: Part2.D2, Part3.D2
  N33: Part2.D3_PWM, Part3.D3
  N34: Part2.D4, Part3.D4
  N35: Part2.D5_PWM, Part3.D5
  N36: Part2.D6_PWM, Part3.D6
  N37: Part2.D7, Part3.D7
  N38: Part2.RESET, Part3.RST
  3V3: Part2.3V3, Part3.3V3
  5V: Part2.5V, Part3.5V
  VIN: Part2.VIN, Part3.VIN
  N39: Part3.D0, U1.P
  N40: Part6.TXD, Part8.D0(RX)
  N41: Part6.RXD, R2.Pin_1, R3.Pin_0
  N42: Part6.VCC, Part8.N$178
  N43: Part6.GND, Part8.N$118, R2.Pin_0
  N44: RE1.EncoderPinA, Part8.N$77
  N45: RE1.EncoderPinC, Part8.N$87
  N46: RE1.EncoderPinB, Part8.D11
  N47: Part8.D1(TX), R3.Pin_1
  N48: Part8.D2, RE4.EncoderPinA
  N49: Part8.N$48, RE4.EncoderPinB
  N50: Part8.N$55, RE4.EncoderPinC

notes:
  Encoder #2 to help wheels turn at the same rate so the robot goes straight
  Encoder #1 to help wheels turn at the same rate so the robot goes straight
  LCD Display with I2C interface, represented by the perfboard, enables the LCD to run on 2 analog pins
  HC-05 Bluetooth for wireless communication between gyroscopic controller and robot
  Prototyping shield is detached from the motor shield to help display wiring
  LM35 Temperature Sensor
